# Fritzing sketch Scheme (saved by Fritzing 0.9.3b)

parts:
  PIC_16F877A1 = PIC 16F877A [package=THT]
  LED1 = smd LED [color="Red (633nm)" package="0603 [SMD]"]
  U1 = LCD-16X2 [package=lcd-16x2_noholes]
  Часть1 = Gas Sensor Breakout Board
  R1 = Resistor [tolerance=±5% resistance=10k package=THT]

nets:
  5V: PIC_16F877A1.MCLR, U1.VDD, Часть1.A1, Часть1.A2, Часть1.H1
  N1: PIC_16F877A1.RA0/AN0, Часть1.B1
  N2: PIC_16F877A1.RA1/AN1, LED1.anode
  N3: PIC_16F877A1.RD1/PSP1, U1.RS
  N4: PIC_16F877A1.RD2/PSP2, U1.R_W
  N5: PIC_16F877A1.RD3/PSP3, U1.E
  N6: PIC_16F877A1.RB0/INT, U1.DB0
  N7: PIC_16F877A1.RB1, U1.DB1
  N8: PIC_16F877A1.RB2, U1.DB2
  N9: PIC_16F877A1.RB3, U1.DB3
  N10: PIC_16F877A1.RB4, U1.DB4
  N11: PIC_16F877A1.RB5, U1.DB5
  N12: PIC_16F877A1.RB6, U1.DB6
  N13: PIC_16F877A1.RB7, U1.DB7
  GND: LED1.cathode, U1.VSS, U1.VO, Часть1.GND, R1.Pin_1
  N14: Часть1.B2, R1.Pin_0

// code stored in the sketch: Fucking_program.ino
'?? ???? ?? ? ??????? MQ-135 ??????????? ????? ? ???????? ??????????,
'??????????????? ???????????? ??2 ? ????????? ? ???????? ?????????? ?
'??????? ?????????? ?? LCD ? ? UART.

'PIC16F877A
'open Tools->LCD Module
'open Tools->Microcontroller View
'change analog Ra0

'????????? ???


'????????? LCD ?????? ??? ????? ????????????????
Define LCD_LINES = 2  '?????????? ????? ? LCD
Define LCD_CHARS = 16  '?????????? ????????  ? LCD
Define LCD_BITS = 8  '???? ?????? 8-? ??????
Define LCD_DREG = PORTB  '???? ?????? ?????? ?? LCD
Define LCD_DBIT = 0  '?????? 4 ?????? ?????
Define LCD_RSREG = PORTD  '???? ?????? ??????????? ?? ???? RS LCD
Define LCD_RSBIT = 1  '????? ?????? ??????????? ?? ???? RS LCD
Define LCD_EREG = PORTD  '???? ?????? ??????????? ?? ???? E LCD
Define LCD_EBIT = 3  '????? ?????? ??????????? ?? ???? E LCD
Define LCD_RWREG = PORTD  '???? ?????? ??????????? ?? ???? RW LCD
Define LCD_RWBIT = 2  '????? ?????? ??????????? ?? ???? RW LCD


TRISA = %00000001  '???????????????? PORTA (?????/??????)
ADCON1 = %00000010  '????????????? ??? ?????? PORTA ??? ??????????

Dim pin_mq135 As Long  '???????? ?????????? ??????????? ???? c ????????

Lcdinit 1  '???????????????? ??????? LCD
Lcddefchar 2, %0, %0, %0, %11100, %100, %11100, %10000, %11100

loop:  '???? ? ???? ?????????
Adcin 0, pin_mq135  '????? ???????? ? ??????????? ????? A0

Lcdout "   Conc. CO", 2, ": "
Lcdcmdout LcdLine2Home  '???????????????? ??????? ?? ?????? ?????? LCD
Lcdout "    ", #pin_mq135, " ", "ppm"

loopend:

WaitMs 100
Lcdcmdout LcdClear  '???????? ?????

Goto loop  '????? ?? ???? ?????????

// code stored in the sketch: Fucking_Program_(alpha).bas
'На базе МК и датчика MQ-135 разработать схему и прошивку устройства,
'контролирующего концентрацию СО2 в помещении с цветовой индикацией и
'выводом информации на LCD и в UART.

'PIC16F877A

Hseropen 9600  'Открытие аппаратного порта UART на скорости передачи данных 9600

'Настройка LCD модуля под порты микроконтроллера
Define LCD_LINES = 2  'Количество строк в LCD
Define LCD_CHARS = 16  'Количество символов  в LCD
Define LCD_BITS = 8  'Шина данных 8-х битная
Define LCD_DREG = PORTB  'Порт вывода данных на LCD
Define LCD_DBIT = 0  'Первые 4 вывода порта
Define LCD_RSREG = PORTD  'Порт вывода контроллера на вход RS LCD
Define LCD_RSBIT = 1  'Номер вывода контроллера на вход RS LCD
Define LCD_EREG = PORTD  'Порт вывода контроллера на вход E LCD
Define LCD_EBIT = 3  'Номер вывода контроллера на вход E LCD
Define LCD_RWREG = PORTD  'Порт вывода контроллера на вход RW LCD
Define LCD_RWBIT = 2  'Номер вывода контроллера на вход RW LCD

Symbol warning_led = PORTA.1  'Присвоим выводу PORTA.1 имя Warning_led

TRISA = %00000001  'Конфигурирование PORTA (входы/выходы)
ADCON1 = %00000010  'Устанавливаем все выводы PORTA как аналоговые

Lcdinit 1  'инициализировали коретку LCD
Lcddefchar 2, %0, %0, %0, %11100, %100, %11100, %10000, %11100  'Создание пользовательского сивола для вывода на LCD с идентификатором 2
'''''''''''''''''''''''''''''''''''''''''''''''''''''''''''''''''''''''''''
'------ Fucking constants from mq135 library for arduino ------'
Const adc_value_max = 1024  'Максимальное значение АЦП
Const operating_voltage = 5  'Напряжение питания датчика
Const rl_board = 10  'kOm - Резистор нагрузки на плате датчика
Const r_zero = 76.63  'Om - Сопротивление датчика на открытом воздухе
'Параметры для рассчёта ppm CO2 относительно сопротивления датчика (вычислены по графикам в Datasheet)
Const par_a = -0.42
Const par_b = 1.92
'Параметры схемы
Dim pin_mq135 As Long  'Создание переменной аналогового пина c датчиком
Dim sensor_voltage As Single  'Создание переменной текущего напряжения, снимаемого с датчика
Dim sensor_resistance As Single  'Создание переменной текущего сопротивления датчика
Dim concentration_co2 As Single  'Создание переменной текущей концентрации CO2
'''''''''''''''''''''''''''''''''''''''''''''''''''''''''''''''''''''''''''

loop:  'Вход в тело программы
Adcin 0, pin_mq135  'Сняли значения с аналогового порта A0
sensor_voltage = pin_mq135 * (operating_voltage / adc_value_max)  'Вычисление напряжения, поступаемого на пин An0
sensor_resistance = (operating_voltage - sensor_voltage) / sensor_voltage * rl_board  'Вычисление сопротивления датчика

concentration_co2 = Exp((Log(sensor_resistance / r_zero) - par_b) / par_a)  'Вычисление концентрации CO2

Hserout "Concentration CO2: ", #concentration_co2, CrLf  'Отправка значения концентрации в аппаратный порт UART
Serout PORTC.0, 9600, "Concentration CO2: ", #concentration_co2, CrLf  'Отправка значения концентрации в программный порт UART

Lcdout "   Conc. CO", 2, ": "  'Вывод первой строчки на LCD, здсь 2 - заранее созданный символ
Lcdcmdout LcdLine2Home  'Инициализировали коретку на вторую строку LCD
Lcdout " ", #concentration_co2, " ", "ppm"

If concentration_co2 > 1000 'Устанавливаем условие, по статистическим данным допустимая концентрация CO2 в воздухе не должна превышать 1000 ppm
Then  
warning_led = 1  'Подача питания на порт со светодиодом
Hserout "ПРЕВЫШЕНИЕ ДОПУСТИМОЙ КОНЦЕНТРАЦИИ CO2!!!", CrLf  'Отправка значения концентрации в аппаратный порт UART
Serout PORTC.0, 9600, "ПРЕВЫШЕНИЕ ДОПУСТИМОЙ КОНЦЕНТРАЦИИ CO2!!!", CrLf  'Отправка значения концентрации в программный порт UART
Else
warning_led = 0  'Выключение светодиода
Endif

loopend:

WaitMs 100
Lcdcmdout LcdClear  'Очистка LCD

Goto loop  'Возвращение в начало тела программы
